# Fritzing sketch Aquastop (saved by Fritzing 0.9.3b)
breadboards: 1

parts:
  Power_plug1 = Power plug
  C1 = Electrolytic Capacitor [capacitance=10µF package="100 mil [THT, electrolytic]"]
  M1 = DC Motor
  R2 = PHOTOCELL [package=photocell-kit]
  IC1 = Hex Inverter Schmitt Trigger SN74HC14 [package="DIP (Dual Inline)"]  # not connected
  Q1 = TRANSISTOR_NPN [package=to-92-ammo]
  U1 = mystery part, 4 pins [chip_label=AC-DC]
  U2 = mystery part, 6 pins [chip_label=30A]
  R4 = Resistor [tolerance=±5% resistance=10k package=THT]
  R3 = Resistor [tolerance=±5% resistance=330 package=THT]
  R1 = Resistor [tolerance=±5% resistance=10k package=THT]

nets:
  N1: Power_plug1.GND, M1.pin_2, U1.pin4
  N2: Power_plug1.VCC, U1.pin3, U2.pin6
  N3: C1.-, U1.pin2, U2.pin2, R1.Pin_0
  N4: C1.+, Q1.E, R1.Pin_1
  N5: M1.pin_1, U2.pin5
  N6: R2.P$1, U1.pin1, U2.pin1, R3.Pin_0
  N7: R2.P$2, R4.Pin_0
  N8: Q1.B, R4.Pin_1
  N9: Q1.C, R3.Pin_1
