# Fritzing sketch ENC28J60 (saved by Fritzing 0.9.2b)

parts:
  Part1 = Arduino Uno (Rev3)
  U3 = mystery part, 12 pins [chip_label=ENC28J60]

nets:
  N1: Part1.D8, U3.pin8
  N2: Part1.D11_PWM/MOSI, U3.pin9
  N3: Part1.D12/MISO, U3.pin3
  N4: Part1.D13/SCK, U3.pin4
  N5: Part1.GND, U3.pin7
  N6: Part1.3V3, U3.pin6
