# Fritzing sketch Meteostation (saved by Fritzing 0.9.2b)
breadboards: 1

parts:
  Part1 = Arduino Uno (Rev3)
  DHT1 = DHT11 Humitidy and Temperature Sensor
  U1 = mystery part, 5 pins [chip_label=TGS4161]
  C2 = Tantalum Capacitor [capacitance=0.1µF package="B 3528 [SMD, tantalum]"]
  C1 = Tantalum Capacitor [capacitance=0.33mF package="B 3528 [SMD, tantalum]"]
  U2 = Voltage Regulator - 5V [package="DPak [SMD]"]
  U3 = mystery part, 12 pins [chip_label=ENC28J60]
  U4 = mystery part, 4 pins [chip_label=bmp180]
  R1 = Resistor [tolerance=±5% resistance=10k package=THT]

nets:
  N1: Part1.A0, U1.pin3
  N2: Part1.A4/SDA, U4.pin4
  N3: Part1.A5/SCL, U4.pin3
  N4: Part1.D8, U3.pin8
  N5: Part1.D11_PWM/MOSI, U3.pin9
  N6: Part1.D12/MISO, U3.pin3
  N7: Part1.D13/SCK, U3.pin4
  GND: Part1.GND, DHT1.GND, U1.pin2, C2.-, C1.-, U2.GND, U3.pin7, U4.pin2
  N8: Part1.D2, DHT1.DATA, R1.Pin_0
  N9: Part1.3V3, U3.pin6
  5V: Part1.5V, DHT1.VDD, C1.+, U2.input_voltage, U4.pin1, R1.Pin_1
  N10: U1.pin5, C2.+, U2.output_voltage

custom parts:
  DHT11 Humitidy and Temperature Sensor: DHT11 Humidity and Temperature Sensor
