# Fritzing sketch bmp180 (saved by Fritzing 0.9.2b)
breadboards: 1

parts:
  Part1 = Arduino Uno (Rev3)
  U4 = mystery part, 4 pins [chip_label=bmp180]

nets:
  N1: Part1.A4/SDA, U4.pin4
  N2: Part1.A5/SCL, U4.pin3
  N3: Part1.GND, U4.pin2
  N4: Part1.5V, U4.pin1
