# Fritzing sketch link (saved by Fritzing 0.9.0b)
breadboards: 1

parts:
  U1 = HC-SR04 [chip_label=IC package="SIP (Single Inline) [THT]"]
  Part1 = Arduino Uno (Rev3)
  R2 = Resistor [tolerance=±5% resistance=220 package="1206 [SMD]"]
  LED4 = smd LED [color="Yellow (592nm)" package="1206 [SMD]"]
  J1 = Piezo Speaker

nets:
  VCC: U1.Vcc, Part1.5V, R2.Pin_0
  N1: U1.Trig, Part1.D12/MISO
  N2: U1.Echo, Part1.D11_PWM/MOSI
  GND: U1.GND, Part1.GND, J1.pin1
  N3: Part1.D9_PWM, LED4.anode, J1.pin2
  N4: R2.Pin_1, LED4.cathode

custom parts:
  HC-SR04: HC-SR04 ultrasound distance sensor
