# Fritzing sketch Meteostation (saved by Fritzing 0.9.0b)
breadboards: 1

parts:
  Part1 = Arduino Uno (Rev3)
  LED1 = LED - 5mm [color="Green (570nm)" package="5 mm [THT]"]
  U1 = mystery part, 5 pins [chip_label=TGS4161]
  R1 = Resistor [tolerance=±5% resistance=330 package=THT]

nets:
  N1: Part1.A3, U1.pin3
  N2: Part1.GND, LED1.cathode, U1.pin4
  N3: Part1.5V, U1.pin1
  N4: LED1.anode, R1.Pin_1
  N5: U1.pin2, R1.Pin_0
