# Fritzing sketch tgs4161 (saved by Fritzing 0.9.2b)
breadboards: 1

parts:
  Part1 = Arduino Uno (Rev3)
  U1 = mystery part, 5 pins [chip_label=TGS4161]
  C2 = Tantalum Capacitor [capacitance=0.1µF package="B 3528 [SMD, tantalum]"]
  U2 = Voltage Regulator - 5V [package="DPak [SMD]"]
  C1 = Tantalum Capacitor [capacitance=0.33mF package="B 3528 [SMD, tantalum]"]

nets:
  N1: Part1.A0, U1.pin3
  GND: Part1.GND, U1.pin2, C2.-, U2.GND, C1.-
  N2: Part1.5V, U2.input_voltage, C1.+
  N3: U1.pin5, C2.+, U2.output_voltage
